# Fritzing sketch air-quality (saved by Fritzing 1.0.2b)
breadboards: 1

parts:
  Uno = Arduino Uno (Rev3)
  Wyświetlacz_LCD = Grove OLED 128x96
  Czujnik_Gazu_MQ-135 = MQ-4
  Moduł_WiFi = ESP8266-01S [part_number=ESP8266]
  R9 = Resistor [tolerance=±5% power=0.25W resistance=10k package=THT]
  Czujnik_ciśnienia_GY-68 = Barometric Pressure Sensor - BMP180 Breakout (GY-68)
  R7 = Resistor [tolerance=±5% power=0.25W resistance=1k package=THT]
  R8 = Resistor [tolerance=±5% power=0.25W resistance=1k package=THT]

nets (from the breadboard view):
  N1: Uno.A0, Czujnik_Gazu_MQ-135.AO
  N2: Uno.A4/SDA, Wyświetlacz_LCD.SDA, Czujnik_ciśnienia_GY-68.SDA
  N3: Uno.A5/SCL, Wyświetlacz_LCD.SCL, Czujnik_ciśnienia_GY-68.SCL
  GND: Uno.GND, Uno.D0/RX, Wyświetlacz_LCD.GND, Czujnik_Gazu_MQ-135.GND, Moduł_WiFi.GND, Czujnik_ciśnienia_GY-68.GND, R7.Pin_1, R8.Pin_1
  N4: Uno.D1/TX, Moduł_WiFi.TXD
  N5: Uno.D2, Czujnik_Gazu_MQ-135.DO
  N6: Uno.RESET, Moduł_WiFi.RST
  N7: Uno.3V3, R9.Pin_0
  VCC: Uno.5V, Wyświetlacz_LCD.VCC, Czujnik_Gazu_MQ-135.VCC, Czujnik_ciśnienia_GY-68.VCC
  N8: Moduł_WiFi.RXD, R7.Pin_0, R8.Pin_0
  N9: Moduł_WiFi.VCC, Moduł_WiFi.CH_PD, R9.Pin_1

notes:
  Czujnik gazu MQ-135
  Ekran LCD
  Moduł WiFi ESP8266
  Czujnik ciśnienia GY-86
